# Fritzing sketch CO2-Sensor (saved by Fritzing 0.9.4)

parts:
  WeMos_D1_Mini1 = WeMos D1 Mini
  37mm_LED_Ring = 12 NeoPixel Ring [part_number=1643]
  K1 = CO2 sensor [package=PCB]

nets:
  5V: WeMos_D1_Mini1.5V, 37mm_LED_Ring.VDD, K1.G+
  N1: WeMos_D1_Mini1.D1, K1.I2C_SCL
  N2: WeMos_D1_Mini1.D2, K1.I2C_SDA
  N3: WeMos_D1_Mini1.D3, 37mm_LED_Ring.IN
  N4: WeMos_D1_Mini1.G, 37mm_LED_Ring.GND, K1.G0

custom parts:
  12 NeoPixel Ring: 12 ultra bright smart LED NeoPixels are arranged in a circle with 1.5" (37mm) outer diameter. The rings are 'chainable' - connect the output pin of one to the input pin of another. Use only one microcontroller pin to control as many as you can chain together! Each LED is addressable as the driver chip is inside the LED. Each one has ~18mA constant current drive so the color will be very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
  CO2 sensor: A CO2 sensor from CO2Meter - K30. Datasheet http://co2meters.com/Documentation/Datasheets/DS30-01%20-%20K30.pdf Could not make fine PCB and principal. You should make yours if needed.
