# Fritzing sketch CO2-Sensor (saved by Fritzing 0.9.4)

parts:
  WeMos_D1_Mini1 = WeMos D1 Mini
  CO2_Sensor = SCD30
  37mm_LED_Ring = 12 NeoPixel Ring [part_number=1643]

nets:
  3V3: WeMos_D1_Mini1.3V3, CO2_Sensor.VDD
  5V: WeMos_D1_Mini1.5V, 37mm_LED_Ring.VDD
  N1: WeMos_D1_Mini1.D1, CO2_Sensor.RX/SDA
  N2: WeMos_D1_Mini1.D2, CO2_Sensor.TX/SCL
  N3: WeMos_D1_Mini1.D3, 37mm_LED_Ring.IN
  GND: WeMos_D1_Mini1.G, CO2_Sensor.GND, 37mm_LED_Ring.GND

custom parts:
  SCD30: CO2 , humidity, and temperature sensor * Current consumption: 19 mA @ 1 meas. per 2 s. * Digital interface UART or I2C * Company: Sensirion - The Sensor Company Electrical specifications * average current: 19 mA * max. current: 75 mA * DC supply: 3.3 V - 5.5 V Operation conditions * temperature: 0 – 50°C * humidity: 0 – 95 %RH * sensor lifetime: 15 years CO2-sensor: * NDIR CO 2 sensor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
  12 NeoPixel Ring: 12 ultra bright smart LED NeoPixels are arranged in a circle with 1.5" (37mm) outer diameter. The rings are 'chainable' - connect the output pin of one to the input pin of another. Use only one microcontroller pin to control as many as you can chain together! Each LED is addressable as the driver chip is inside the LED. Each one has ~18mA constant current drive so the color will be very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
