# Fritzing sketch CO2-Sensor (saved by Fritzing 0.9.4)

parts:
  WeMos_D1_Mini1 = WeMos D1 Mini
  37mm_LED_Ring = 12 NeoPixel Ring [part_number=1643]
  MH-Z2 = MH-Z14 [part_number=MH-Z14]

nets:
  5V: WeMos_D1_Mini1.5V, 37mm_LED_Ring.VDD, MH-Z2.1, MH-Z2.15
  N1: WeMos_D1_Mini1.D1, MH-Z2.10, MH-Z2.13
  N2: WeMos_D1_Mini1.D2, MH-Z2.11, MH-Z2.14
  N3: WeMos_D1_Mini1.D3, 37mm_LED_Ring.IN
  N4: WeMos_D1_Mini1.G, 37mm_LED_Ring.GND, MH-Z2.2, MH-Z2.3

custom parts:
  12 NeoPixel Ring: 12 ultra bright smart LED NeoPixels are arranged in a circle with 1.5" (37mm) outer diameter. The rings are 'chainable' - connect the output pin of one to the input pin of another. Use only one microcontroller pin to control as many as you can chain together! Each LED is addressable as the driver chip is inside the LED. Each one has ~18mA constant current drive so the color will be very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
  MH-Z14: MH-Z14 NDIR Infrared gas module is a common type, small size sensor, using non-dispersive infrared (NDIR) principle to detect the existence of CO2 in the air, with good selectivity, non-oxygen dependant, long life. Built-in temperature sensor can do temperature compensation; and it has digital output and analog voltage output.
