# Fritzing sketch CO2-Sensor (saved by Fritzing 0.9.4)

parts:
  WeMos_D1_Mini1 = WeMos D1 Mini
  37mm_LED_Ring = 12 NeoPixel Ring [part_number=1643]
  CCS811 = CJMCU-811

nets:
  3V3: WeMos_D1_Mini1.3V3, CCS811.VCC
  5V: WeMos_D1_Mini1.5V, 37mm_LED_Ring.VDD
  N1: WeMos_D1_Mini1.D1, CCS811.SCL
  N2: WeMos_D1_Mini1.D2, CCS811.SDA
  N3: WeMos_D1_Mini1.D3, 37mm_LED_Ring.IN
  N4: WeMos_D1_Mini1.G, 37mm_LED_Ring.GND

custom parts:
  12 NeoPixel Ring: 12 ultra bright smart LED NeoPixels are arranged in a circle with 1.5" (37mm) outer diameter. The rings are 'chainable' - connect the output pin of one to the input pin of another. Use only one microcontroller pin to control as many as you can chain together! Each LED is addressable as the driver chip is inside the LED. Each one has ~18mA constant current drive so the color will be very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
  CJMCU-811: The CCS811 is an ultra-low power digital gas sensor solution which integrates a metal oxide (MOX) gas sensor to detect a wide range of Volatile Organic Compounds (VOCs) for indoor air quality monitoring with a microcontroller unit (MCU), which includes an Analog-to-Digital converter (ADC), and an I²C interface.
